// Logisim project 16 Bits Adder Funcionall.circ as structural Verilog: 5 circuits, main circuit Complemento de 2 On/Off
module _16_Bits (
  input  [15:0] A,
  input  [15:0] B,
  output Carry,
  output [15:0] out_4
);

  wire full_adder_1_carry_out, full_adder_2_carry_out, full_adder_3_carry_out, full_adder_4_carry_out,
       full_adder_5_carry_out, full_adder_6_carry_out, full_adder_7_carry_out, full_adder_8_carry_out,
       full_adder_9_carry_out, full_adder_10_carry_out, full_adder_11_carry_out, full_adder_12_carry_out,
       full_adder_13_carry_out, full_adder_14_carry_out, half_adder_1_carry;

  Half_Adder half_adder_1 (.in_1(B[0]), .in_2(A[0]), .Saida(out_4[0]), .Carry(half_adder_1_carry));
  Full_Adder full_adder_1 (
    .A(B[1]), .B(A[1]), .Carry(half_adder_1_carry), .Saida(out_4[1]), .Carry_Out(full_adder_1_carry_out));
  Full_Adder full_adder_2 (
    .A(B[2]), .B(A[2]), .Carry(full_adder_1_carry_out), .Saida(out_4[2]), .Carry_Out(full_adder_2_carry_out));
  Full_Adder full_adder_3 (
    .A(B[4]), .B(A[4]), .Carry(full_adder_4_carry_out), .Saida(out_4[4]), .Carry_Out(full_adder_3_carry_out));
  Full_Adder full_adder_4 (
    .A(B[3]), .B(A[3]), .Carry(full_adder_2_carry_out), .Saida(out_4[3]), .Carry_Out(full_adder_4_carry_out));
  Full_Adder full_adder_5 (
    .A(B[5]), .B(A[5]), .Carry(full_adder_3_carry_out), .Saida(out_4[5]), .Carry_Out(full_adder_5_carry_out));
  Full_Adder full_adder_6 (
    .A(B[6]), .B(A[6]), .Carry(full_adder_5_carry_out), .Saida(out_4[6]), .Carry_Out(full_adder_6_carry_out));
  Full_Adder full_adder_7 (
    .A(B[7]), .B(A[7]), .Carry(full_adder_6_carry_out), .Saida(out_4[7]), .Carry_Out(full_adder_7_carry_out));
  Full_Adder full_adder_8 (
    .A(B[8]), .B(A[8]), .Carry(full_adder_7_carry_out), .Saida(out_4[8]), .Carry_Out(full_adder_8_carry_out));
  Full_Adder full_adder_9 (
    .A(B[9]), .B(A[9]), .Carry(full_adder_8_carry_out), .Saida(out_4[9]), .Carry_Out(full_adder_9_carry_out));
  Full_Adder full_adder_10 (
    .A(B[10]), .B(A[10]), .Carry(full_adder_9_carry_out), .Saida(out_4[10]),
    .Carry_Out(full_adder_10_carry_out));
  Full_Adder full_adder_11 (
    .A(B[11]), .B(A[11]), .Carry(full_adder_10_carry_out), .Saida(out_4[11]),
    .Carry_Out(full_adder_11_carry_out));
  Full_Adder full_adder_12 (
    .A(B[12]), .B(A[12]), .Carry(full_adder_11_carry_out), .Saida(out_4[12]),
    .Carry_Out(full_adder_12_carry_out));
  Full_Adder full_adder_13 (
    .A(B[14]), .B(A[14]), .Carry(full_adder_14_carry_out), .Saida(out_4[14]),
    .Carry_Out(full_adder_13_carry_out));
  Full_Adder full_adder_14 (
    .A(B[13]), .B(A[13]), .Carry(full_adder_12_carry_out), .Saida(out_4[13]),
    .Carry_Out(full_adder_14_carry_out));
  Full_Adder full_adder_15 (
    .A(B[15]), .B(A[15]), .Carry(full_adder_13_carry_out), .Saida(out_4[15]), .Carry_Out(Carry));
endmodule

// Half
module Half_Adder (
  input  in_1,
  input  in_2,
  output Saida,
  output Carry
);

  and and_1 (Carry, in_1, in_2);
  xor xor_1 (Saida, in_1, in_2);
endmodule

module Full_Adder (
  input  A,
  input  B,
  input  Carry,
  output Saida,
  output Carry_Out
);

  wire and_1_out, half_adder_1_carry, half_adder_1_saida;

  Half_Adder half_adder_1 (.in_1(A), .in_2(B), .Saida(half_adder_1_saida), .Carry(half_adder_1_carry));
  and and_1 (and_1_out, half_adder_1_saida, Carry);
  xor xor_1 (Saida, half_adder_1_saida, Carry);
  or or_1 (Carry_Out, and_1_out, half_adder_1_carry);
endmodule

module Inversor (
  input  [15:0] A,
  input  Seletor,
  output [15:0] Saida
);

  wire [15:0] n16_bits_1_out_4, not_1_out;

  assign not_1_out = ~A;  // NOT_Gate not_1, 16 bits wide
  _16_Bits u_16_bits_1 (.A(16'h1), .B(not_1_out), .out_4(n16_bits_1_out_4));  // open: Carry
  Multiplexer #(.width(16), .enable("false")) multiplexer_1 (
    .in0(A), .in1(n16_bits_1_out_4), .out(Saida), .sel(Seletor));
endmodule

module Complemento_de_2_On_Off (
  input  [15:0] A,
  input  [15:0] B,
  input  Seletor_A,
  input  Seletor_B,
  output [15:0] Saida,
  output cARRY
);

  wire [15:0] inversor_1_saida, inversor_2_saida;

  Inversor inversor_1 (.A(A), .Seletor(Seletor_A), .Saida(inversor_1_saida));
  Inversor inversor_2 (.A(B), .Seletor(Seletor_B), .Saida(inversor_2_saida));
  _16_Bits u_16_bits_1 (.A(inversor_1_saida), .B(inversor_2_saida), .Carry(cARRY), .out_4(Saida));
endmodule
