// Logisim project Laboratorio 2.circ as structural Verilog: 4 circuits, main circuit MAC
module MAC (
  input  [7:0] in_1,
  input  [7:0] in_2,
  input  Clock,
  output [15:0] out_4
);

  wire [7:0] multiplier_1_cout, multiplier_1_out;
  wire [15:0] register_1_q;

  Multiplier multiplier_1 (.a(in_1), .b(in_2), .out(multiplier_1_out), .cout(multiplier_1_cout));  // open: cin
  Complemento_de_2_On_Off complemento_de_2_on_off_1 (
    .A({multiplier_1_out, multiplier_1_cout}), .B(register_1_q), .Seletor_A(1'b0), .Seletor_B(1'b0),
    .Saida(out_4));  // open: cARRY
  Register #(.width(16)) register_1 (.D(out_4), .Q(register_1_q), .clk(Clock));  // open: en, clr
endmodule

module Memorias (
  input  [3:0] Adress_RAM,
  input  [7:0] XR,
  input  Store,
  input  Clk,
  input  Load,
  input  [3:0] Adress_Rom,
  output [15:0] Filtro
);

  wire [7:0] ram_1_data, rom_1_data;

  RAM #(.addrWidth(4), .bus("separate")) ram_1 (
    .addr(Adress_RAM), .din(XR), .data(ram_1_data), .str(Store), .clk(Clk), .ld(Load));  // open: sel, clr
  ROM #(.addrWidth(4)) rom_1 (.addr(Adress_Rom), .data(rom_1_data));  // open: sel
  MAC mac_1 (.in_1(ram_1_data), .in_2(rom_1_data), .Clock(Clk), .out_4(Filtro));

  // Notes on the sheet:
  //   contents of rom_1 (hex, n*v repeats v):
  //   86 c6 d6 76 a1 64 8c ab b3 a9 8d 64 86 c6 d6 76
endmodule

module Adress_Box (
  input  Clk,
  output [3:0] out_2,
  output [3:0] out_3
);

  wire counter_1_carry, counter_2_carry, counter_3_carry;
  wire [3:0] counter_3_q;

  Counter #(.width(1), .max('h1)) counter_1 (.count(Clk), .carry(counter_1_carry), .clk(Clk));  // open: load, D, Q, clr
  Counter #(.width(4), .max('hf)) counter_2 (
    .count(counter_1_carry), .Q(out_2), .carry(counter_2_carry), .clk(Clk), .clr(counter_2_carry));  // open: load, D
  Counter #(.width(4), .max('hf)) counter_3 (
    .count(counter_1_carry), .Q(counter_3_q), .carry(counter_3_carry), .clk(Clk), .clr(counter_3_carry));  // open: load, D
  assign out_3 = ~counter_3_q;  // NOT_Gate not_1, 4 bits wide
endmodule

module Datapath (
  input  [7:0] in_1,
  output [15:0] y_n
);

  wire clock_1_out;
  wire [3:0] adress_box_1_out_2, adress_box_1_out_3;

  Adress_Box adress_box_1 (.Clk(clock_1_out), .out_2(adress_box_1_out_2), .out_3(adress_box_1_out_3));
  Memorias memorias_1 (
    .Adress_RAM(adress_box_1_out_2), .XR(in_1), .Store(1'b0), .Load(1'b1), .Adress_Rom(adress_box_1_out_3),
    .Clk(clock_1_out), .Filtro(y_n));
  Clock clock_1 (.out(clock_1_out));
endmodule
