// Logisim project Part1_Completa.circ as structural Verilog
module main (
);

  wire caminho_de_controle_1_en_ram, caminho_de_controle_1_rd_ram, caminho_de_controle_1_sel1_bit0,
       caminho_de_controle_1_sel1_bit1, caminho_de_controle_1_sel_ula, caminho_de_controle_1_selop2,
       caminho_de_controle_1_wr_acc, caminho_de_controle_1_wr_ram, clock_1_out;
  wire [5:0] caminho_de_dados_1_control_path;
  wire [23:0] caminho_de_dados_1_ram;
  wire [31:0] caminho_de_controle_1_dout_rom, caminho_de_dados_1_din_ram, mem_1_saida;

  Clock clock_1 (.out(clock_1_out));
  Caminho_de_COntrole caminho_de_controle_1 (
    ._31(caminho_de_dados_1_control_path[5]), ._30(caminho_de_dados_1_control_path[4]),
    ._29(caminho_de_dados_1_control_path[3]), ._28(caminho_de_dados_1_control_path[2]),
    ._27(caminho_de_dados_1_control_path[1]), ._26(caminho_de_dados_1_control_path[0]), .Clock(clock_1_out),
    .EN_RAM(caminho_de_controle_1_en_ram), .WR_RAM(caminho_de_controle_1_wr_ram),
    .RD_RAM(caminho_de_controle_1_rd_ram), .WR_ACC(caminho_de_controle_1_wr_acc),
    .SEL1_BIT1(caminho_de_controle_1_sel1_bit1), .SEL1_BIT0(caminho_de_controle_1_sel1_bit0),
    .DOUT_ROM(caminho_de_controle_1_dout_rom), .SELOp2(caminho_de_controle_1_selop2),
    .SEL_ULA(caminho_de_controle_1_sel_ula));
  Caminho_de_Dados caminho_de_dados_1 (
    .DOUT_ROM(caminho_de_controle_1_dout_rom), .Clock(clock_1_out), .D_OUT_RAM(mem_1_saida),
    .SEL_OP2(caminho_de_controle_1_selop2), .WR_ACC(caminho_de_controle_1_wr_acc),
    .DIN_RAM(caminho_de_dados_1_din_ram), .Control_Path(caminho_de_dados_1_control_path),
    .RAM(caminho_de_dados_1_ram), .Bit0(caminho_de_controle_1_sel1_bit0),
    .Bit1(caminho_de_controle_1_sel1_bit1), .SEL_ULA(caminho_de_controle_1_sel_ula));
  mem mem_1 (
    .Adress(caminho_de_dados_1_ram), .Data_in(caminho_de_dados_1_din_ram),
    .EN_RAM(caminho_de_controle_1_en_ram), .WR_RAM(caminho_de_controle_1_wr_ram), .Clock(clock_1_out),
    .Saida(mem_1_saida), .RD_RAM(caminho_de_controle_1_rd_ram));
endmodule

module mem (
  input  [23:0] Adress,
  input  [31:0] Data_in,
  input  EN_RAM,
  input  RD_RAM,
  input  WR_RAM,
  input  Clock,
  output [31:0] Saida
);

  RAM #(.addrWidth(24), .dataWidth(32), .bus("separate")) ram_1 (
    .addr(Adress), .din(Data_in), .data(Saida), .str(WR_RAM), .sel(EN_RAM), .clk(Clock), .ld(RD_RAM));  // open: clr
endmodule

module Logical (
  input  OP31,
  input  OP30,
  input  OP29,
  input  OP28,
  input  OP27,
  input  OP26,
  output EN_Ram,
  output WR_RAM,
  output RD_RAM,
  output EM_PC,
  output WR_ACC,
  output bit1,
  output bit0,
  output SelOp2,
  output ULA
);

  wire and_1_out, and_2_out, and_3_out, and_5_out, and_6_out, not_1_out, not_2_out, not_3_out;

  not not_1 (not_1_out, OP26);
  not not_2 (not_2_out, OP28);
  not not_3 (not_3_out, OP27);
  and and_1 (and_1_out, OP27, not_1_out);
  and and_2 (and_2_out, OP28, not_1_out);
  and and_3 (and_3_out, not_2_out, not_3_out, OP26);
  and and_4 (WR_RAM, ~OP28, ~OP27, OP26);  // AND_Gate
  and and_5 (and_5_out, OP28, ~OP26);  // AND_Gate
  and and_6 (and_6_out, OP27, ~OP26);  // AND_Gate
  or or_1 (EM_PC, OP26, OP27, OP28);
  or or_2 (WR_ACC, OP27, OP28);
  and and_7 (bit1, ~OP28, OP27, ~OP26);  // AND_Gate
  and and_8 (bit0, ~OP28, OP27, OP26);  // AND_Gate
  and and_9 (SelOp2, OP28, ~OP26);  // AND_Gate
  and and_10 (ULA, OP28, OP27);
  or or_3 (RD_RAM, and_5_out, and_6_out);
  or or_4 (EN_Ram, and_1_out, and_2_out, and_3_out);
endmodule

module ULA (
  input  [31:0] A,
  input  [31:0] B,
  input  SEL_ULA,
  output [31:0] Saida
);

  wire [31:0] adder_1_out, subtractor_1_out;

  Adder #(.width(32)) adder_1 (.a(A), .b(B), .out(adder_1_out));  // open: cin, cout
  Subtractor #(.width(32)) subtractor_1 (.a(A), .b(B), .out(subtractor_1_out));  // open: bin, bout
  Multiplexer #(.width(32), .enable("false")) multiplexer_1 (
    .in0(adder_1_out), .in1(subtractor_1_out), .out(Saida), .sel(SEL_ULA));
endmodule

module MemoriaProg (
  input  [23:0] PC_IN,
  output [31:0] DOUT_ROM
);

  ROM #(.addrWidth(24), .dataWidth(32)) rom_1 (.addr(PC_IN), .data(DOUT_ROM), .sel(1'b1));
endmodule

module PC___4 (
  input  EN_PC,
  input  Clock,
  output [23:0] PC_to_ROM
);

  wire [23:0] adder_1_out;

  Register #(.width(24)) register_1 (.D(adder_1_out), .en(EN_PC), .Q(PC_to_ROM), .clk(Clock));  // open: clr
  Adder #(.width(24)) adder_1 (.a(24'h4), .b(PC_to_ROM), .out(adder_1_out));  // open: cin, cout
endmodule

module Caminho_de_COntrole (
  input  _31,
  input  _30,
  input  _29,
  input  _28,
  input  _27,
  input  _26,
  input  Clock,
  output EN_RAM,
  output WR_RAM,
  output RD_RAM,
  output WR_ACC,
  output SEL1_BIT1,
  output SEL1_BIT0,
  output [31:0] DOUT_ROM,
  output SELOp2,
  output SEL_ULA
);

  wire logical_1_em_pc;
  wire [23:0] pc_4_1_pc_to_rom;

  Logical logical_1 (
    .OP31(_31), .OP30(_30), .OP29(_29), .OP28(_28), .OP27(_27), .OP26(_26), .EN_Ram(EN_RAM), .WR_RAM(WR_RAM),
    .RD_RAM(RD_RAM), .EM_PC(logical_1_em_pc), .WR_ACC(WR_ACC), .bit1(SEL1_BIT1), .bit0(SEL1_BIT0),
    .SelOp2(SELOp2), .ULA(SEL_ULA));
  PC___4 pc_4_1 (.EN_PC(logical_1_em_pc), .Clock(Clock), .PC_to_ROM(pc_4_1_pc_to_rom));
  MemoriaProg memoriaprog_1 (.PC_IN(pc_4_1_pc_to_rom), .DOUT_ROM(DOUT_ROM));
endmodule

module Caminho_de_Dados (
  input  [31:0] DOUT_ROM,
  input  Clock,
  input  [31:0] D_OUT_RAM,
  input  SEL_OP2,
  input  Bit0,
  input  WR_ACC,
  input  Bit1,
  input  SEL_ULA,
  output [5:0] Control_Path,
  output [23:0] RAM,
  output [31:0] DIN_RAM
);

  wire [31:0] ir_1_go_2_system, multiplexer_1_out, multiplexer_2_out, ula_1_saida;

  Multiplexer #(.width(32), .enable("false")) multiplexer_1 (
    .in0(D_OUT_RAM), .in1(ir_1_go_2_system), .out(multiplexer_1_out), .sel(SEL_OP2));
  IR ir_1 (
    .D_OUT_ROM(DOUT_ROM), .Clock(Clock), .Go_2_Control(Control_Path), .Go_2_RAM(RAM),
    .Go_2_System(ir_1_go_2_system));
  ACC acc_1 (.ACC_IN(multiplexer_2_out), .WR_ACC(WR_ACC), .Clock(Clock), .ACC_OUT(DIN_RAM));
  Multiplexer #(.select(2), .width(32), .enable("false")) multiplexer_2 (
    .in0(D_OUT_RAM), .in1(ir_1_go_2_system), .in2(ula_1_saida), .out(multiplexer_2_out), .sel({Bit1, Bit0}));  // open: in3
  ULA ula_1 (.A(multiplexer_1_out), .B(DIN_RAM), .Saida(ula_1_saida), .SEL_ULA(SEL_ULA));
endmodule

module IR (
  input  [31:0] D_OUT_ROM,
  input  Clock,
  output [5:0] Go_2_Control,
  output [23:0] Go_2_RAM,
  output [31:0] Go_2_System
);

  wire [25:24] register_1_q;

  Register #(.width(32)) register_1 (
    .D(D_OUT_ROM), .Q({Go_2_Control, register_1_q, Go_2_RAM}), .clk(Clock));  // open: en, clr

  assign Go_2_System = {{8{1'b0}}, Go_2_RAM};
endmodule

module ACC (
  input  [31:0] ACC_IN,
  input  WR_ACC,
  input  Clock,
  output [31:0] ACC_OUT
);

  wire [31:0] adder_1_out;

  Register #(.width(32)) register_1 (.D(adder_1_out), .en(WR_ACC), .Q(ACC_OUT), .clk(Clock));  // open: clr
  Adder #(.width(32)) adder_1 (.a(ACC_OUT), .b(ACC_IN), .out(adder_1_out));  // open: cin, cout
endmodule
