// Logisim project Part2_Completa.circ as structural Verilog: 11 circuits, main circuit main
module main (
);

  wire caminho_de_controle_1_en_mon, caminho_de_controle_1_en_ram, caminho_de_controle_1_en_tec,
       caminho_de_controle_1_rd_ram, caminho_de_controle_1_sel_bit0, caminho_de_controle_1_sel_bit1,
       caminho_de_controle_1_sel_op2, caminho_de_controle_1_sel_ula, caminho_de_controle_1_wr_acc,
       caminho_de_controle_1_wr_ram, clock_1_out;
  wire [5:0] caminho_de_dados_1_control_path;
  wire [6:0] teclado_1_dout_tec;
  wire [23:0] caminho_de_dados_1_add_imediato;
  wire [31:0] caminho_de_controle_1_dout_rom, caminho_de_dados_1_din_bus, mem_1_dout_bus;

  Clock clock_1 (.out(clock_1_out));
  Caminho_de_COntrole caminho_de_controle_1 (
    ._31(caminho_de_dados_1_control_path[5]), ._30(caminho_de_dados_1_control_path[4]),
    ._29(caminho_de_dados_1_control_path[3]), ._28(caminho_de_dados_1_control_path[2]),
    ._27(caminho_de_dados_1_control_path[1]), ._26(caminho_de_dados_1_control_path[0]), .Clock(clock_1_out),
    .SEL_OP2(caminho_de_controle_1_sel_op2), .SEL_ULA(caminho_de_controle_1_sel_ula),
    .EN_TEC(caminho_de_controle_1_en_tec), .EN_MON(caminho_de_controle_1_en_mon),
    .ADD_IMEDIATO(caminho_de_dados_1_add_imediato), .DOUT_ROM(caminho_de_controle_1_dout_rom),
    .RD_RAM(caminho_de_controle_1_rd_ram), .WR_ACC(caminho_de_controle_1_wr_acc),
    .WR_RAM(caminho_de_controle_1_wr_ram), .EN_RAM(caminho_de_controle_1_en_ram),
    .SEL_BIT1(caminho_de_controle_1_sel_bit1), .SEL_BIT0(caminho_de_controle_1_sel_bit0));
  Teclado teclado_1 (
    .DIN_BUS(caminho_de_dados_1_din_bus[6:0]), .EN_MON(caminho_de_controle_1_en_mon), .Clock(clock_1_out),
    .EN_Tec(caminho_de_controle_1_en_tec), .DOUT_TEC(teclado_1_dout_tec));
  Caminho_de_Dados caminho_de_dados_1 (
    .DOUT_ROM(caminho_de_controle_1_dout_rom), .Clock(clock_1_out), .D_OUT_TEC(teclado_1_dout_tec),
    .D_OUT_BUS(mem_1_dout_bus), .SEL_OP2(caminho_de_controle_1_sel_op2),
    .WR_ACC(caminho_de_controle_1_wr_acc), .DIN_BUS(caminho_de_dados_1_din_bus),
    .Control_Path(caminho_de_dados_1_control_path), .ADD_IMEDIATO(caminho_de_dados_1_add_imediato),
    .Bit0(caminho_de_controle_1_sel_bit0), .Bit1(caminho_de_controle_1_sel_bit1),
    .SEL_ULA(caminho_de_controle_1_sel_ula));
  mem mem_1 (
    .ADD_IMED(caminho_de_dados_1_add_imediato), .DIN_BUSS(caminho_de_dados_1_din_bus),
    .EN_RAM(caminho_de_controle_1_en_ram), .WR_RAM(caminho_de_controle_1_wr_ram), .Clock(clock_1_out),
    .DOUT_BUS(mem_1_dout_bus), .RD_RAM(caminho_de_controle_1_rd_ram));
endmodule

module mem (
  input  [23:0] ADD_IMED,
  input  [31:0] DIN_BUSS,
  input  EN_RAM,
  input  RD_RAM,
  input  WR_RAM,
  input  Clock,
  output [31:0] DOUT_BUS
);

  RAM #(.addrWidth(24), .dataWidth(32), .bus("separate")) ram_1 (
    .addr(ADD_IMED), .din(DIN_BUSS), .data(DOUT_BUS), .str(WR_RAM), .sel(EN_RAM), .clk(Clock), .ld(RD_RAM),
    .clr(1'b0));
endmodule

module Logical (
  input  OP30,
  input  B___OP28,
  input  D___OP26,
  input  OP31,
  input  A___OP29,
  input  C___OP27,
  output EN_PC,
  output RD_RAM,
  output WR_ACC,
  output WR_RAM,
  output EN_RAM,
  output SEL_OP1_Bit1,
  output SEL_OP1_Bit0,
  output SEL_OP2,
  output SEL_ULA,
  output EN_TEC,
  output EN_MON,
  output SEL_JUMP
);

  wire and_1_out, and_2_out, and_3_out, and_4_out, and_5_out, and_6_out, and_12_out, and_13_out, and_14_out,
       or_4_out;

  and and_1 (and_1_out, ~A___OP29, C___OP27);  // AND_Gate
  and and_2 (and_2_out, A___OP29, D___OP26);
  and and_3 (and_3_out, A___OP29, ~C___OP27, D___OP26);  // AND_Gate
  and and_4 (and_4_out, ~A___OP29, ~B___OP28, C___OP27, ~D___OP26);  // AND_Gate
  and and_5 (and_5_out, ~A___OP29, ~B___OP28, C___OP27, D___OP26);  // AND_Gate
  and and_6 (and_6_out, A___OP29, ~C___OP27);  // AND_Gate
  and and_7 (SEL_OP2, B___OP28, ~D___OP26);  // AND_Gate
  and and_8 (SEL_ULA, B___OP28, C___OP27);
  and and_9 (EN_TEC, A___OP29, D___OP26);
  and and_10 (EN_MON, A___OP29, C___OP27);
  and and_11 (SEL_JUMP, A___OP29, ~C___OP27, ~D___OP26);  // AND_Gate
  or or_1 (WR_ACC, B___OP28, and_1_out, and_2_out);
  or or_2 (SEL_OP1_Bit1, and_3_out, and_4_out);
  or or_3 (SEL_OP1_Bit0, and_5_out, and_6_out);
  and and_12 (and_12_out, ~D___OP26, ~C___OP27, ~B___OP28, ~A___OP29);  // AND_Gate
  or or_4 (or_4_out, D___OP26, C___OP27, B___OP28, A___OP29);
  and and_13 (and_13_out, B___OP28, ~D___OP26);  // AND_Gate
  and and_14 (and_14_out, ~A___OP29, C___OP27, ~D___OP26);  // AND_Gate
  and and_15 (WR_RAM, ~A___OP29, ~B___OP28, D___OP26, ~C___OP27);  // AND_Gate
  or or_5 (EN_PC, and_12_out, or_4_out);
  or or_6 (RD_RAM, and_13_out, and_14_out);
  or or_7 (EN_RAM, WR_RAM, RD_RAM);
endmodule

module ULA (
  input  [31:0] A,
  input  [31:0] B,
  input  SEL_ULA,
  output [31:0] Saida
);

  wire [31:0] adder_1_out, subtractor_1_out;

  Adder #(.width(32)) adder_1 (.a(A), .b(B), .out(adder_1_out));  // open: cin, cout
  Subtractor #(.width(32)) subtractor_1 (.a(A), .b(B), .out(subtractor_1_out));  // open: bin, bout
  Multiplexer #(.width(32), .enable("false")) multiplexer_1 (
    .in0(adder_1_out), .in1(subtractor_1_out), .out(Saida), .sel(SEL_ULA));
endmodule

module MemoriaProg (
  input  [23:0] PC_IN,
  output [31:0] DOUT_ROM
);

  ROM #(.addrWidth(24), .dataWidth(32)) rom_1 (.addr(PC_IN), .data(DOUT_ROM), .sel(1'b1));

  // Notes on the sheet:
  //   contents of rom_1 (hex, n*v repeats v):
  //   0 0 0 100100 101000 0 0 0 10100 0 0 0 100100 0 0 0 10 1000
endmodule

module PC___4 (
  input  EN_PC,
  input  Clock,
  input  Clear,
  input  [23:0] ADD_IMEDIATO,
  input  SEL_JUMP,
  output [23:0] PC_to_ROM
);

  wire [23:0] adder_1_out, multiplexer_1_out;

  Register #(.width(24)) register_1 (.D(adder_1_out), .en(EN_PC), .Q(PC_to_ROM), .clk(Clock), .clr(Clear));
  Adder #(.width(24)) adder_1 (.a(24'h1), .b(multiplexer_1_out), .out(adder_1_out));  // open: cin, cout
  Multiplexer #(.width(24), .enable("false")) multiplexer_1 (
    .in0(PC_to_ROM), .in1(ADD_IMEDIATO), .out(multiplexer_1_out), .sel(SEL_JUMP));
endmodule

module Caminho_de_COntrole (
  input  _31,
  input  _30,
  input  _29,
  input  [23:0] ADD_IMEDIATO,
  input  _28,
  input  _27,
  input  _26,
  input  Clock,
  output SEL_OP2,
  output SEL_ULA,
  output EN_TEC,
  output EN_MON,
  output [31:0] DOUT_ROM,
  output RD_RAM,
  output WR_ACC,
  output WR_RAM,
  output EN_RAM,
  output SEL_BIT1,
  output SEL_BIT0
);

  wire logical_1_en_pc, logical_1_sel_jump;
  wire [23:0] pc_4_1_pc_to_rom;

  Logical logical_1 (
    .OP31(_31), .OP30(_30), .A___OP29(_29), .B___OP28(_28), .C___OP27(_27), .D___OP26(_26),
    .EN_PC(logical_1_en_pc), .RD_RAM(RD_RAM), .WR_ACC(WR_ACC), .WR_RAM(WR_RAM), .EN_RAM(EN_RAM),
    .SEL_OP1_Bit1(SEL_BIT1), .SEL_OP1_Bit0(SEL_BIT0), .SEL_OP2(SEL_OP2), .SEL_ULA(SEL_ULA), .EN_TEC(EN_TEC),
    .EN_MON(EN_MON), .SEL_JUMP(logical_1_sel_jump));
  PC___4 pc_4_1 (
    .EN_PC(logical_1_en_pc), .Clock(Clock), .Clear(1'b0), .ADD_IMEDIATO(ADD_IMEDIATO),
    .SEL_JUMP(logical_1_sel_jump), .PC_to_ROM(pc_4_1_pc_to_rom));
  MemoriaProg memoriaprog_1 (.PC_IN(pc_4_1_pc_to_rom), .DOUT_ROM(DOUT_ROM));
endmodule

module Caminho_de_Dados (
  input  [31:0] DOUT_ROM,
  input  Clock,
  input  [6:0] D_OUT_TEC,
  input  [31:0] D_OUT_BUS,
  input  SEL_OP2,
  input  Bit0,
  input  WR_ACC,
  input  Bit1,
  input  SEL_ULA,
  output [5:0] Control_Path,
  output [23:0] ADD_IMEDIATO,
  output [31:0] DIN_BUS
);

  wire [31:0] bit_extender_1_out, ir_1_go_2_system, multiplexer_1_out, multiplexer_2_out, ula_1_saida;

  assign bit_extender_1_out = {{25{1'b0}}, D_OUT_TEC};  // Bit_Extender bit_extender_1
  Multiplexer #(.width(32), .enable("false")) multiplexer_1 (
    .in0(D_OUT_BUS), .in1(ir_1_go_2_system), .out(multiplexer_1_out), .sel(SEL_OP2));
  IR ir_1 (
    .D_OUT_ROM(DOUT_ROM), .Clock(Clock), .Go_2_Control(Control_Path), .Go_2_RAM(ADD_IMEDIATO),
    .Go_2_System(ir_1_go_2_system));
  ACC acc_1 (.ACC_IN(multiplexer_2_out), .WR_ACC(WR_ACC), .Clock(Clock), .ACC_OUT(DIN_BUS));
  Multiplexer #(.select(2), .width(32), .enable("false")) multiplexer_2 (
    .in0(D_OUT_BUS), .in1(bit_extender_1_out), .in2(ir_1_go_2_system), .in3(ula_1_saida),
    .out(multiplexer_2_out), .sel({Bit1, Bit0}));
  ULA ula_1 (.A(multiplexer_1_out), .B(DIN_BUS), .Saida(ula_1_saida), .SEL_ULA(SEL_ULA));
endmodule

module IR (
  input  [31:0] D_OUT_ROM,
  input  Clock,
  output [5:0] Go_2_Control,
  output [23:0] Go_2_RAM,
  output [31:0] Go_2_System
);

  wire [25:24] register_1_q;

  Register #(.width(32)) register_1 (
    .D(D_OUT_ROM), .en(1'b1), .Q({Go_2_Control, register_1_q, Go_2_RAM}), .clk(Clock), .clr(1'b0));

  assign Go_2_System = {{8{1'b0}}, Go_2_RAM};
endmodule

module ACC (
  input  [31:0] ACC_IN,
  input  WR_ACC,
  input  Clock,
  output [31:0] ACC_OUT
);

  wire [31:0] adder_1_out;

  Register #(.width(32)) register_1 (.D(adder_1_out), .en(WR_ACC), .Q(ACC_OUT), .clk(Clock), .clr(1'b0));
  Adder #(.width(32)) adder_1 (.a(ACC_OUT), .b(ACC_IN), .out(adder_1_out));  // open: cin, cout
endmodule

module Teclado (
  input  [6:0] DIN_BUS,
  input  EN_MON,
  input  Clock,
  input  EN_Tec,
  output [6:0] DOUT_TEC
);

  TTY tty_1 (.data(DIN_BUS), .clk(Clock), .we(EN_MON), .clr(1'b0));
  Keyboard #(.buflen(7)) keyboard_1 (.clk(Clock), .re(EN_Tec), .clr(1'b0), .data(DOUT_TEC));  // open: avail
endmodule
